// Logisim project lab2.circ as structural Verilog
module question1 (
  input  A1,
  input  A0,
  input  B1,
  input  B0,
  input  [3:0] in_5,
  input  [1:0] a,
  input  [1:0] b,
  output \output ,
  output out_9
);

  wire and_1_out, and_2_out, and_3_out, and_4_out, and_5_out, not_1_out, not_2_out, not_3_out, not_4_out,
       not_5_out;

  not not_1 (not_1_out, A1);
  and and_1 (and_1_out, not_1_out, not_2_out);
  not not_2 (not_2_out, A0);
  not not_3 (not_3_out, A1);
  and and_2 (and_2_out, not_3_out, B0);
  not not_4 (not_4_out, A1);
  and and_3 (and_3_out, not_4_out, B1);
  not not_5 (not_5_out, A0);
  and and_4 (and_4_out, not_5_out, B1);
  and and_5 (and_5_out, B1, B0);
  Multiplexer #(.select(4), .enable("false")) multiplexer_1 (
    .in0(1'b1), .in1(1'b1), .in2(1'b1), .in3(1'b1), .in4(1'b0), .in5(1'b1), .in6(1'b1), .in7(1'b1),
    .in8(1'b0), .in9(1'b0), .in10(1'b1), .in11(1'b1), .in12(1'b0), .in13(1'b0), .in14(1'b0), .in15(1'b1),
    .out(out_9), .sel(in_5));
  or or_1 (\output , and_1_out, and_2_out, and_3_out, and_4_out, and_5_out);
  ROM #(.addrWidth(4), .dataWidth(1)) rom_1 (.addr({a, b}));  // open: data, sel
endmodule

module question2 (
  input  X,
  input  Y,
  input  Z,
  input  [2:0] XYZ,
  input  X_2,
  input  Y_2,
  input  Z_2,
  output \output ,
  output out_9
);

  wire and_1_out, and_2_out, and_3_out, not_1_out, not_2_out, not_3_out, not_4_out, not_5_out, not_6_out;

  not not_1 (not_1_out, X);
  not not_2 (not_2_out, Y);
  not not_3 (not_3_out, X);
  not not_4 (not_4_out, Z);
  not not_5 (not_5_out, Y);
  not not_6 (not_6_out, Z);
  Multiplexer #(.select(3), .enable("false")) multiplexer_1 (
    .in0(1'b1), .in1(1'b1), .in2(1'b1), .in3(1'b0), .in4(1'b1), .in5(1'b0), .in6(1'b0), .in7(1'b0),
    .out(out_9), .sel(XYZ));
  and and_1 (and_1_out, not_1_out, not_2_out);
  and and_2 (and_2_out, not_3_out, not_4_out);
  and and_3 (and_3_out, not_5_out, not_6_out);
  or or_1 (\output , and_1_out, and_2_out, and_3_out);
  ROM #(.addrWidth(3), .dataWidth(1)) rom_1 (.addr({X_2, Y_2, Z_2}));  // open: data, sel

  // Notes on the sheet:
  //   contents of rom_1 (hex, n*v repeats v):
  //   1 1 1 0 1
endmodule
