// Logisim project lab3.circ as structural Verilog: 1 circuit, main circuit main
module main (
  input  [1:0] \input ,
  output [2:0] \return ,
  output vend
);

  wire clock_1_out;
  wire [2:0] state_q;
  wire [6:4] rom_1_data;

  Clock clock_1 (.out(clock_1_out));
  ROM #(.addrWidth(5), .dataWidth(7)) rom_1 (
    .addr({state_q, \input }), .data({rom_1_data, vend, \return }));  // open: sel
  Register #(.width(3)) state (.D(rom_1_data), .Q(state_q), .clk(clock_1_out));  // open: en, clr

  // Notes on the sheet:
  //   contents of rom_1 (hex, n*v repeats v):
  //   0 10 20 8
endmodule
